# Fritzing sketch hello_gpio_control (saved by Fritzing 1.0.0rc)
breadboards: 1

parts:
  Mod1 = Raspberry Pi 4B
  S1 = Round Pushbutton
  Q1 = TRANSISTOR_NPN [package=to-92-ammo]
  VCC1 = Battery block 9V
  U1 = RELAY-SOLIDSTATE [package=relay-s108t02]

nets:
  N1: Mod1.3V3, S1.leg0
  N2: Mod1.GPIO2, Q1.B
  N3: Mod1.GND, Q1.C, VCC1.-
  N4: Mod1.GPIO21, S1.leg1
  N5: Q1.E, U1.-
  N6: VCC1.+, U1.+

notes:
  light bulb
